// Logisim project 4b.circ as structural Verilog: 1 circuit, main circuit main
module main (
  input  Cin,
  input  E,
  input  F,
  output SUM,
  output Cout
);

  wire and_1_out, and_2_out, xor_1_out;

  xor xor_1 (xor_1_out, E, F);
  and and_1 (and_1_out, F, E);
  xor xor_2 (SUM, Cin, xor_1_out);
  and and_2 (and_2_out, Cin, xor_1_out);
  or or_1 (Cout, and_2_out, and_1_out);
endmodule
