// Logisim project 5.circ as structural Verilog: 1 circuit, main circuit main
module main (
  input  G,
  input  H,
  output I,
  output L,
  output J,
  output K,
  output M
);

  wire not_1_out, not_2_out;

  not not_1 (not_1_out, G);
  not not_2 (not_2_out, H);
  and and_1 (J, not_1_out, H);
  and and_2 (I, G, H);
  and and_3 (K, not_1_out, not_2_out);
  or or_1 (L, I, J);
  or or_2 (M, L, K);
endmodule
