// Logisim project RGB.circ as structural Verilog: 1 circuit, main circuit main
module main (
  input  Z,
  input  Y,
  input  X,
  input  W
);

  wire and_1_out, and_2_out, nor_1_out, nor_2_out, or_1_out, or_2_out, or_3_out, xor_1_out, xor_2_out;

  xor xor_1 (xor_1_out, Y, W);
  or or_1 (or_1_out, W, X);
  nor nor_1 (nor_1_out, xor_1_out, Z);
  and and_1 (and_1_out, or_1_out, Z);
  nor nor_2 (nor_2_out, Z, Y);
  and and_2 (and_2_out, Z, X);
  or or_2 (or_2_out, nor_1_out, and_1_out);
  or or_3 (or_3_out, nor_2_out, and_2_out);
  xor xor_2 (xor_2_out, X, W);
  // RGBLED rgbled_1: pin names not known; wires that end beside it: xor_2_out, or_2_out, or_3_out
endmodule
