// Logisim project LED_matrix_template.circ as structural Verilog: 1 circuit, main circuit main
module main (
);

  wire and_1_out, and_2_out, and_3_out, and_4_out, and_5_out, and_6_out, and_7_out, and_8_out, and_9_out,
       and_10_out, and_11_out, and_12_out, and_13_out, and_14_out, and_15_out, and_16_out, and_17_out,
       and_18_out, and_19_out, and_20_out, and_21_out, and_22_out, and_23_out, and_24_out, and_25_out,
       not_1_out, not_2_out, not_3_out, not_4_out, not_5_out, not_6_out, not_7_out, not_8_out, not_9_out,
       not_10_out, not_11_out, not_12_out, not_13_out, not_14_out, not_15_out, not_16_out, not_17_out,
       not_18_out, not_19_out, not_20_out, not_21_out, not_22_out, not_23_out, not_24_out, not_25_out,
       pull_resistor_1_node, pull_resistor_2_node, pull_resistor_3_node, pull_resistor_4_node,
       pull_resistor_5_node, pull_resistor_6_node, pull_resistor_7_node, pull_resistor_8_node,
       pull_resistor_9_node, pull_resistor_10_node;

  Pull_Resistor pull_resistor_1 (.node(pull_resistor_1_node));
  Pull_Resistor pull_resistor_2 (.node(pull_resistor_2_node));
  Pull_Resistor pull_resistor_3 (.node(pull_resistor_3_node));
  Pull_Resistor pull_resistor_4 (.node(pull_resistor_4_node));
  Pull_Resistor pull_resistor_5 (.node(pull_resistor_5_node));
  LED led_1 (.in(and_1_out));
  and and_1 (and_1_out, pull_resistor_1_node, not_1_out);
  not not_1 (not_1_out, pull_resistor_6_node);
  LED led_2 (.in(and_2_out));
  and and_2 (and_2_out, pull_resistor_2_node, not_2_out);
  not not_2 (not_2_out, pull_resistor_6_node);
  LED led_3 (.in(and_3_out));
  and and_3 (and_3_out, pull_resistor_3_node, not_3_out);
  not not_3 (not_3_out, pull_resistor_6_node);
  LED led_4 (.in(and_4_out));
  and and_4 (and_4_out, pull_resistor_4_node, not_4_out);
  not not_4 (not_4_out, pull_resistor_6_node);
  LED led_5 (.in(and_5_out));
  and and_5 (and_5_out, pull_resistor_5_node, not_5_out);
  not not_5 (not_5_out, pull_resistor_6_node);
  LED led_6 (.in(and_6_out));
  and and_6 (and_6_out, pull_resistor_1_node, not_6_out);
  not not_6 (not_6_out, pull_resistor_7_node);
  LED led_7 (.in(and_7_out));
  and and_7 (and_7_out, pull_resistor_2_node, not_7_out);
  not not_7 (not_7_out, pull_resistor_7_node);
  LED led_8 (.in(and_8_out));
  and and_8 (and_8_out, pull_resistor_3_node, not_8_out);
  not not_8 (not_8_out, pull_resistor_7_node);
  LED led_9 (.in(and_9_out));
  and and_9 (and_9_out, pull_resistor_4_node, not_9_out);
  not not_9 (not_9_out, pull_resistor_7_node);
  LED led_10 (.in(and_10_out));
  and and_10 (and_10_out, pull_resistor_5_node, not_10_out);
  not not_10 (not_10_out, pull_resistor_7_node);
  LED led_11 (.in(and_11_out));
  and and_11 (and_11_out, pull_resistor_1_node, not_11_out);
  not not_11 (not_11_out, pull_resistor_8_node);
  LED led_12 (.in(and_12_out));
  and and_12 (and_12_out, pull_resistor_2_node, not_12_out);
  not not_12 (not_12_out, pull_resistor_8_node);
  LED led_13 (.in(and_13_out));
  and and_13 (and_13_out, pull_resistor_3_node, not_13_out);
  not not_13 (not_13_out, pull_resistor_8_node);
  LED led_14 (.in(and_14_out));
  and and_14 (and_14_out, pull_resistor_4_node, not_14_out);
  not not_14 (not_14_out, pull_resistor_8_node);
  LED led_15 (.in(and_15_out));
  and and_15 (and_15_out, pull_resistor_5_node, not_15_out);
  not not_15 (not_15_out, pull_resistor_8_node);
  Pull_Resistor #(.pull(1)) pull_resistor_6 (.node(pull_resistor_6_node));
  Pull_Resistor #(.pull(1)) pull_resistor_7 (.node(pull_resistor_7_node));
  Pull_Resistor #(.pull(1)) pull_resistor_8 (.node(pull_resistor_8_node));
  Pull_Resistor #(.pull(1)) pull_resistor_9 (.node(pull_resistor_9_node));
  Pull_Resistor #(.pull(1)) pull_resistor_10 (.node(pull_resistor_10_node));
  LED led_16 (.in(and_16_out));
  and and_16 (and_16_out, pull_resistor_1_node, not_16_out);
  not not_16 (not_16_out, pull_resistor_9_node);
  LED led_17 (.in(and_17_out));
  and and_17 (and_17_out, pull_resistor_2_node, not_17_out);
  not not_17 (not_17_out, pull_resistor_9_node);
  LED led_18 (.in(and_18_out));
  and and_18 (and_18_out, pull_resistor_3_node, not_18_out);
  not not_18 (not_18_out, pull_resistor_9_node);
  LED led_19 (.in(and_19_out));
  and and_19 (and_19_out, pull_resistor_4_node, not_19_out);
  not not_19 (not_19_out, pull_resistor_9_node);
  LED led_20 (.in(and_20_out));
  and and_20 (and_20_out, pull_resistor_5_node, not_20_out);
  not not_20 (not_20_out, pull_resistor_9_node);
  LED led_21 (.in(and_21_out));
  and and_21 (and_21_out, pull_resistor_1_node, not_21_out);
  not not_21 (not_21_out, pull_resistor_10_node);
  LED led_22 (.in(and_22_out));
  and and_22 (and_22_out, pull_resistor_2_node, not_22_out);
  not not_22 (not_22_out, pull_resistor_10_node);
  LED led_23 (.in(and_23_out));
  and and_23 (and_23_out, pull_resistor_3_node, not_23_out);
  not not_23 (not_23_out, pull_resistor_10_node);
  LED led_24 (.in(and_24_out));
  and and_24 (and_24_out, pull_resistor_4_node, not_24_out);
  not not_24 (not_24_out, pull_resistor_10_node);
  LED led_25 (.in(and_25_out));
  and and_25 (and_25_out, pull_resistor_5_node, not_25_out);
  not not_25 (not_25_out, pull_resistor_10_node);

  // Notes on the sheet:
  //   COLUMNS
  //   ROWS
endmodule
