// Logisim project counters.circ as structural Verilog: 1 circuit, main circuit main
module main (
);

  wire and_1_out, and_2_out, and_3_out, and_4_out, clock_1_out, clock_2_out, j_k_ff_1_qn, j_k_ff_2_q,
       j_k_ff_3_q, j_k_ff_3_qn, j_k_ff_4_q, j_k_ff_5_qn, j_k_ff_6_q, j_k_ff_7_q, j_k_ff_8_q;

  J_K_Flip_Flop j_k_ff_1 (
    .J(1'b1), .K(1'b1), .clk(clock_1_out), .Qn(j_k_ff_1_qn), .reset(and_3_out));  // open: Q, preset
  Clock clock_1 (.out(clock_1_out));
  J_K_Flip_Flop j_k_ff_2 (
    .J(1'b1), .K(1'b1), .clk(clock_2_out), .Q(j_k_ff_2_q), .reset(and_4_out));  // open: Qn, preset
  Clock clock_2 (.out(clock_2_out));
  J_K_Flip_Flop j_k_ff_3 (
    .J(1'b1), .K(1'b1), .clk(j_k_ff_1_qn), .Q(j_k_ff_3_q), .Qn(j_k_ff_3_qn), .reset(and_3_out));  // open: preset
  J_K_Flip_Flop j_k_ff_4 (
    .J(j_k_ff_2_q), .K(j_k_ff_2_q), .clk(clock_2_out), .Q(j_k_ff_4_q), .reset(and_4_out));  // open: Qn, preset
  J_K_Flip_Flop j_k_ff_5 (
    .J(1'b1), .K(1'b1), .clk(j_k_ff_3_qn), .Qn(j_k_ff_5_qn), .reset(and_3_out));  // open: Q, preset
  and and_1 (and_1_out, j_k_ff_2_q, j_k_ff_4_q);
  J_K_Flip_Flop j_k_ff_6 (
    .J(and_1_out), .K(and_1_out), .clk(clock_2_out), .Q(j_k_ff_6_q), .reset(and_4_out));  // open: Qn, preset
  J_K_Flip_Flop j_k_ff_7 (
    .J(1'b1), .K(1'b1), .clk(j_k_ff_5_qn), .Q(j_k_ff_7_q), .reset(and_3_out));  // open: Qn, preset
  and and_2 (and_2_out, j_k_ff_2_q, j_k_ff_4_q, j_k_ff_6_q);
  and and_3 (and_3_out, j_k_ff_3_q, j_k_ff_7_q);
  J_K_Flip_Flop j_k_ff_8 (
    .J(and_2_out), .K(and_2_out), .clk(clock_2_out), .Q(j_k_ff_8_q), .reset(and_4_out));  // open: Qn, preset
  and and_4 (and_4_out, j_k_ff_8_q, j_k_ff_4_q);
endmodule
