// Logisim project custom3bit.circ as structural Verilog: 1 circuit, main circuit main
module main (
);

  wire A_q, A_qn, B_q, C_q, clock_1_out, or_1_out, xor_1_out, xor_2_out;

  Clock clock_1 (.out(clock_1_out));
  D_Flip_Flop A (.D(or_1_out), .clk(clock_1_out), .Q(A_q), .Qn(A_qn));  // open: preset, reset
  or or_1 (or_1_out, xor_2_out, A_qn);
  D_Flip_Flop B (.D(A_qn), .clk(clock_1_out), .Q(B_q));  // open: Qn, preset, reset
  xor xor_1 (xor_1_out, A_q, C_q);
  xor xor_2 (xor_2_out, C_q, B_q);
  D_Flip_Flop C (.D(xor_1_out), .clk(clock_1_out), .Q(C_q));  // open: Qn, preset, reset
endmodule
