// Logisim project stopwatch.circ as structural Verilog: 1 circuit, main circuit main
module main (
);

  wire and_1_out, button_1_out, button_2_out, cd4029_3_carry_out, clock_1_out, d_ff_1_q, d_ff_2_q, or_1_out;
  wire [3:0] cd4029_1_q1, cd4029_2_q1, cd4029_3_q1;

  Clock #(.highDuration(10), .lowDuration(10)) clock_1 (.out(clock_1_out));
  Hex_Digit_Display hex_digit_display_1 (.value(cd4029_1_q1));  // open: dp
  Button button_1 (.out(button_1_out));
  or or_1 (or_1_out, button_1_out, and_1_out);
  CD4029 cd4029_1 (
    .BINARY_DECADE(1'b0), .PRESET_ENABLE(button_1_out), .CARRY_IN(1'b0), .UP_DOWN(1'b1), .CLOCK(and_1_out),
    .JAM_1(1'b0), .JAM_2(1'b0), .JAM_3(1'b0), .JAM_4(1'b0), .Q1(cd4029_1_q1[0]), .Q2(cd4029_1_q1[1]),
    .Q3(cd4029_1_q1[2]), .Q4(cd4029_1_q1[3]));  // open: CARRY_OUT
  Hex_Digit_Display hex_digit_display_2 (.value(cd4029_2_q1));  // open: dp
  and and_1 (and_1_out, cd4029_2_q1[1], cd4029_2_q1[2]);
  CD4029 cd4029_2 (
    .BINARY_DECADE(1'b0), .PRESET_ENABLE(or_1_out), .CARRY_IN(cd4029_3_carry_out), .UP_DOWN(1'b1),
    .CLOCK(clock_1_out), .JAM_1(1'b0), .JAM_2(1'b0), .JAM_3(1'b0), .JAM_4(1'b0), .Q1(cd4029_2_q1[0]),
    .Q2(cd4029_2_q1[1]), .Q3(cd4029_2_q1[2]), .Q4(cd4029_2_q1[3]));  // open: CARRY_OUT
  Button button_2 (.out(button_2_out));
  D_Flip_Flop d_ff_1 (.D(d_ff_2_q), .clk(button_2_out), .Q(d_ff_1_q));  // open: Qn, preset, reset
  Hex_Digit_Display hex_digit_display_3 (.value(cd4029_3_q1));  // open: dp
  D_Flip_Flop d_ff_2 (.D(d_ff_1_q), .clk(button_2_out), .Q(d_ff_2_q));  // open: Qn, preset, reset
  CD4029 cd4029_3 (
    .BINARY_DECADE(1'b0), .PRESET_ENABLE(button_1_out), .CARRY_IN(d_ff_1_q), .UP_DOWN(1'b1),
    .CLOCK(clock_1_out), .CARRY_OUT(cd4029_3_carry_out), .JAM_1(1'b0), .JAM_2(1'b0), .JAM_3(1'b0),
    .JAM_4(1'b0), .Q1(cd4029_3_q1[0]), .Q2(cd4029_3_q1[1]), .Q3(cd4029_3_q1[2]), .Q4(cd4029_3_q1[3]));
endmodule
